# Fritzing sketch Sketch_8_ultrasonic_leds (saved by Fritzing 0.9.3b)
breadboards: 1

parts:
  hc-sr1 = hc-sr04
  Part2 = Arduino Uno (Rev3)
  R9 = Resistor [tolerance=±5% resistance=1k package=THT]
  R10 = Resistor [tolerance=±5% resistance=1k package=THT]
  R11 = Resistor [tolerance=±5% resistance=1k package=THT]
  R12 = Resistor [tolerance=±5% resistance=1k package=THT]
  R13 = Resistor [tolerance=±5% resistance=1k package=THT]
  R14 = Resistor [tolerance=±5% resistance=1k package=THT]
  LED8 = LED - 5mm [color="Red (633nm)" package="5 mm [THT]"]
  LED9 = LED - 5mm [color="Red (633nm)" package="5 mm [THT]"]
  LED10 = LED - 5mm [color="Red (633nm)" package="5 mm [THT]"]
  LED11 = LED - 5mm [color="Red (633nm)" package="5 mm [THT]"]
  LED12 = LED - 5mm [color="Red (633nm)" package="5 mm [THT]"]
  LED13 = LED - 5mm [color="Red (633nm)" package="5 mm [THT]"]

nets:
  VCC: hc-sr1.VCC, Part2.5V
  N1: hc-sr1.Trig, Part2.D9_PWM
  N2: hc-sr1.Echo, Part2.D8
  GND: hc-sr1.GND, Part2.GND, LED8.cathode, LED9.cathode, LED10.cathode, LED11.cathode, LED12.cathode, LED13.cathode
  N3: Part2.D2, R9.Pin_1
  N4: Part2.D3_PWM, R10.Pin_1
  N5: Part2.D4, R11.Pin_1
  N6: Part2.D5_PWM, R12.Pin_1
  N7: Part2.D6_PWM, R13.Pin_1
  N8: Part2.D7, R14.Pin_1
  N9: R9.Pin_0, LED8.anode
  N10: R10.Pin_0, LED9.anode
  N11: R11.Pin_0, LED10.anode
  N12: R12.Pin_0, LED11.anode
  N13: R13.Pin_0, LED12.anode
  N14: R14.Pin_0, LED13.anode
